# Fritzing sketch station_7_def_circuit (saved by Fritzing 0.9.3b)
breadboards: 1

parts:
  Part1 = Bare Conductive Touch Board
  Part2 = Lithium Ion Polymer Battery 3.7v 2000mAh [part_number=2011]  # not connected
  J2 = Basic Servo
  VCC1 = Battery
  VCC2 = Battery
  J1 = Basic Servo

nets:
  GND: Part1.GND, J2.gnd, VCC2.-, J1.gnd
  VCC: J2.vcc, VCC1.+, J1.vcc
  N1: VCC1.-, VCC2.+

notes:
  to the copperfoil capacitive sensor
  to 3.5mm audio output jack
  TouchBoard powered by the LiPo battery
  penguin servo
  chimes servo

custom parts:
  Lithium Ion Polymer Battery 3.7v 2000mAh: Lithium ion polymer (also known as 'lipo' or 'lipoly') batteries are thin, light and powerful. The output ranges from 4.2V when completely charged to 3.7V. This battery has a capacity of 2000mAh. The batteries come pre-attached with a genuine 2-pin JST-PH connector as shown and include the necessary protection circuitry.
